// Logisim project m1_37069.circ as structural Verilog
module NotGate (
  input  x,
  output xNOT
);

  Pull_Resistor pull_resistor_1 (.node(xNOT));
  Transistor transistor_1 (.in(1'b1), .out(xNOT), .gate(x));
endmodule

module NorGate (
  input  x,
  input  y,
  output xNORy
);

  wire transistor_1_out;

  Transistor transistor_1 (.in(1'b1), .out(transistor_1_out), .gate(x));
  Pull_Resistor pull_resistor_1 (.node(xNORy));
  Transistor transistor_2 (.in(transistor_1_out), .out(xNORy), .gate(y));
endmodule

module AndGate (
  input  x,
  input  y,
  output xANDy
);

  wire notgate_1_xnot, notgate_2_xnot, transistor_1_out;

  NotGate notgate_1 (.x(x), .xNOT(notgate_1_xnot));
  Transistor transistor_1 (.in(1'b1), .out(transistor_1_out), .gate(notgate_1_xnot));
  NotGate notgate_2 (.x(y), .xNOT(notgate_2_xnot));
  Transistor transistor_2 (.in(transistor_1_out), .out(xANDy), .gate(notgate_2_xnot));
  Pull_Resistor pull_resistor_1 (.node(xANDy));
endmodule

module OrGate (
  input  x,
  input  y,
  output xNORy
);

  wire pull_resistor_1_node, transistor_1_out;

  Transistor transistor_1 (.in(1'b1), .out(transistor_1_out), .gate(x));
  Pull_Resistor pull_resistor_1 (.node(pull_resistor_1_node));
  Transistor transistor_2 (.in(transistor_1_out), .out(pull_resistor_1_node), .gate(y));
  NotGate notgate_1 (.x(pull_resistor_1_node), .xNOT(xNORy));
endmodule
